// Digital circuit cntr.dig as structural Verilog
module cntr (
  input  C,
  input  RST,
  output Q_3,
  output Q_2,
  output Q_1,
  output Q_0
);

  wire nq_0n, nq_1n, nq_2n, nq_3n, undriven, undriven_2, undriven_3, undriven_4, undriven_5, undriven_6,
       undriven_7, undriven_8, undriven_9, undriven_10, undriven_11, undriven_12;

  sg13g2_nand4_1 sg13g2_nand4_1_1 (.A(Q_0), .B(Q_1), .C(Q_2), .D(nq_3n));  // open: Y
  sg13g2_nand2_1 sg13g2_nand2_1_1 (.A(nq_0n), .B(Q_3));  // open: Y
  sg13g2_nand2_1 sg13g2_nand2_1_2 (.A(nq_1n), .B(Q_3));  // open: Y
  sg13g2_nand2_1 sg13g2_nand2_1_3 (.A(nq_2n), .B(Q_3));  // open: Y
  sg13g2_nand3_1 sg13g2_nand3_1_1 (.A(Q_0), .B(Q_1), .C(nq_2n));  // open: Y
  sg13g2_nand2_1 sg13g2_nand2_1_4 (.A(nq_0n), .B(Q_2));  // open: Y
  sg13g2_nand2_1 sg13g2_nand2_1_5 (.A(nq_1n), .B(Q_2));  // open: Y
  sg13g2_nand2_1 sg13g2_nand2_1_6 (.A(Q_0), .B(nq_1n));  // open: Y
  sg13g2_nand2_1 sg13g2_nand2_1_7 (.A(nq_0n), .B(Q_1));  // open: Y
  sg13g2_nand4_1 sg13g2_nand4_1_2 (.A(undriven_5), .B(undriven), .C(undriven_6), .D(undriven_9));  // open: Y
  sg13g2_nand3_1 sg13g2_nand3_1_2 (.A(undriven_2), .B(undriven_3), .C(undriven_7));  // open: Y
  sg13g2_nand2_1 sg13g2_nand2_1_8 (.A(undriven_4), .B(undriven_8));  // open: Y
  sg13g2_dfrbp_1 sg13g2_dfrbp_1_1 (.CLK(C), .D(undriven_12), .Reset(RST), .Q(Q_3), .nQ(nq_3n));
  sg13g2_dfrbp_1 sg13g2_dfrbp_1_2 (.CLK(C), .D(undriven_10), .Reset(RST), .Q(Q_2), .nQ(nq_2n));
  sg13g2_dfrbp_1 sg13g2_dfrbp_1_3 (.CLK(C), .D(undriven_11), .Reset(RST), .Q(Q_1), .nQ(nq_1n));
  sg13g2_dfrbp_1 sg13g2_dfrbp_1_4 (.CLK(C), .D(nq_0n), .Reset(RST), .Q(Q_0), .nQ(nq_0n));

  // Other names for the same wires on the sheet: q_0n = Q_0; q_1n = Q_1; q_2n = Q_2; q_3n = Q_3
endmodule

/* Test case:
           C Q_3 Q_2 Q_1 Q_0
repeat(16) C bits(4,n+1)
*/
