// Digital circuit cells.dig as structural Verilog
module cells (
);

  sg13g2_nor2_1 sg13g2_nor2_1_1 ();  // open: A, B, Y
  sg13g2_xor2_1 sg13g2_xor2_1_1 ();  // open: A, B, Y
  // sg13g2_xnor2_1 sg13g2_xnor2_1_1: pin names not known
  sg13g2_nor3_1 sg13g2_nor3_1_1 ();  // open: A, B, C, Y
  sg13g2_nand4_1 sg13g2_nand4_1_1 ();  // open: A, B, C, D, Y
  sg13g2_nor2b_1 sg13g2_nor2b_1_1 ();  // open: A, B, Y
  sg13g2_or3_1 sg13g2_or3_1_1 ();  // open: A, B, C, Y
  sg13g2_or2_1 sg13g2_or2_1_1 ();  // open: A, B, Y
  sg13g2_nor4_1 sg13g2_nor4_1_1 ();  // open: A, B, C, D, Y
  sg13g2_nand3_1 sg13g2_nand3_1_1 ();  // open: A, B, C, Y
  sg13g2_mux2_1 sg13g2_mux2_1_1 ();  // open: A_0, A_1, S, Y
  sg13g2_mux4_1 sg13g2_mux4_1_1 ();  // open: A_0, A_1, S_0, A_2, A_3, S_1, Y
  sg13g2_or4_1 sg13g2_or4_1_1 ();  // open: A, B, C, D, Y
  sg13g2_nand2_1 sg13g2_nand2_1_1 ();  // open: A, B, Y
  sg13g2_a21o_1 sg13g2_a21o_1_1 ();  // open: A_1, A_2, B_1, Y
  sg13g2_a21oi_1 sg13g2_a21oi_1_1 ();  // open: A_1, A_2, B_1, Y
  sg13g2_o21ai_1 sg13g2_o21ai_1_1 ();  // open: A_1, A_2, B_1, Y
  sg13g2_a22oi_1 sg13g2_a22oi_1_1 ();  // open: A_1, A_2, B_1, B_2, Y
  sg13g2_inv_1 sg13g2_inv_1_1 ();  // open: A, Y
  sg13g2_einvn_2 sg13g2_einvn_2_1 ();  // open: A, TE_B, Z
  sg13g2_ebufn_2 sg13g2_ebufn_2_1 ();  // open: A, TE_B, Z
  sg13g2_a221oi_1 sg13g2_a221oi_1_1 ();  // open: A_1, A_2, B_1, B_2, C_1, Y
  sg13g2_dfrbp_1 sg13g2_dfrbp_1_1 ();  // open: CLK, D, Reset, Q, nQ
  sg13g2_nand3b_1 sg13g2_nand3b_1_1 ();  // open: A_N, B, C, Y

  // Notes on the sheet:
  //   some of the IHP130 standard cells
endmodule
