// Digital circuit sg13g2_a21oi_1.dig as structural Verilog
module sg13g2_a21oi_1 (
  input  A_1,
  input  A_2,
  input  B_1,
  output Y
);

  wire and_1_out;

  and and_1 (and_1_out, A_1, A_2);
  nor nor_1 (Y, and_1_out, B_1);
endmodule
