// Digital circuit sg13g2_a221oi_1.dig as structural Verilog
module sg13g2_a221oi_1 (
  input  A_1,
  input  A_2,
  input  B_1,
  input  B_2,
  input  C_1,
  output Y
);

  wire and_1_out, and_2_out;

  and and_1 (and_1_out, A_1, A_2);
  and and_2 (and_2_out, B_1, B_2);
  nor nor_1 (Y, and_1_out, and_2_out, C_1);
endmodule
