// Digital circuit sg13g2_einvn_2.dig as structural Verilog
module sg13g2_einvn_2 (
  input  A,
  input  TE_B,
  output Z
);

  DriverInvSel #(.invertDriverOutput("true")) driverinvsel_1 (.in(A), .en(TE_B));  // open: out
endmodule
