// Digital circuit sg13g2_mux4_1.dig as structural Verilog
module sg13g2_mux4_1 (
  input  A_0,
  input  A_1,
  input  S_0,
  input  A_2,
  input  A_3,
  input  S_1,
  output Y
);

  Multiplexer #(.Selector_Bits(2)) multiplexer_1 (
    .sel({S_1, S_0}), .in_0(A_0), .in_1(A_1), .in_2(A_2), .in_3(A_3), .out(Y));
endmodule
