// Digital circuit sg13g2_dfrbp_1.dig as structural Verilog
module sg13g2_dfrbp_1 (
  input  CLK,
  input  D,
  input  Reset,
  output Q,
  output nQ
);

  D_FF_AS d_ff_as_1 (.Set(1'b0), .D(D), .C(CLK), .Clr(Reset), .Q(Q), .nQ(nQ));
endmodule
