// Digital circuit sg13g2_mux2_1.dig as structural Verilog
module sg13g2_mux2_1 (
  input  A_0,
  input  A_1,
  input  S,
  output Y
);

  Multiplexer multiplexer_1 (.sel(S), .in_0(A_0), .in_1(A_1), .out(Y));
endmodule
