// Digital circuit sg13g2_o21ai_1.dig as structural Verilog
module sg13g2_o21ai_1 (
  input  A_1,
  input  A_2,
  input  B_1,
  output Y
);

  wire or_1_out;

  or or_1 (or_1_out, A_1, A_2);
  nand nand_1 (Y, or_1_out, B_1);
endmodule
